// Digital circuit ECM-16 computer.dig as structural Verilog
module ECM_16_computer (
  input  Clk,
  input  [31:0] DMA,
  input  [7:0] \int ,
  input  in_4,
  output [15:0] bus,
  output gpr7_latch
);

  wire and_1_out, Byte, clk_stop, delay_1_out, dis_addr_set, disable_SD, E1, E2, E3, E4, E5, E6, INSTR_8,
       Int_mock_out, L0, L1, L2, L3, L4, L5, L6, L7, L8, nclk, not_2_out, not_4_out, not_5_out, not_6_out,
       not_7_out, not_8_out, nr, or_2_out, prefix, pullup_2_out, S0, S4, S5, S6, S7, S8, S11, S12,
       sequencer_1_p6, sequencer_1_p8, sequencer_1_p9, sequencer_1_p10, sequencer_1_p11, sequencer_1_p12,
       sequencer_1_p13, sequencer_1_p14, sequencer_1_p16, sequencer_1_p17, sequencer_1_p18, sequencer_1_p19,
       sequencer_1_p20, sequencer_1_p21, sequencer_1_p22, sequencer_1_p23, Soft_Int, t_b_sel_1_bottom,
       undriven;
  wire [1:0] LA34, S3, S9, S10;
  wire [1:1] not_3_out;
  wire [2:0] caclulating_core_interface_1_dest, caclulating_core_interface_1_function,
       caclulating_core_interface_1_src1, caclulating_core_interface_1_src2;
  wire [3:0] dest_mod, main_alu_no_indicators_1_c, multiplexer_4_out, ROM_address, sequencer_1_p15, src_mod,
       Status_Register_flags_out;
  wire [7:0] _1_to_8b_extender_1_out, _1_to_8b_extender_2_out, caclulating_core_interface_1_const, clk_cnt,
       EA1_i, Instruction_Register_d_out, int_number_d_out, LA1_i, multiplexer_10_out, S1_i, S2_i;
  wire [7:6] en;
  wire [8:0] caclulating_core_interface_1_carry;
  wire [11:11] latch;
  wire [15:0] _1_to_16b_extender_1_out, _16MB_RAM_d, address_adder_1_out, address_adder_1_out_2,
       IV_base_d_out, MDB_d_out, MemPointers_mp_h, MemPointers_mp_l, multiplexer_1_out, multiplexer_2_out,
       multiplexer_3_out, multiplexer_5_out, multiplexer_6_out, pullup_1_out, register_file_1_src1_out,
       register_file_1_src1_to_bus, register_file_1_src2_out;
  wire [15:9] Instruction_Register_d_out_2;
  wire [16:0] caclulating_core_interface_1_nr_o;
  wire [31:0] BP, FP, MABH_d_out, multiplexer_7_out, multiplexer_8_out, multiplexer_9_out,
       multiplexer_11_out, PC, SP;
  wire [63:0] R0_3, R4_7;

  Caclulating_core_interface caclulating_core_interface_1 (
    .nr_o(caclulating_core_interface_1_nr_o[0]), .clk_o(caclulating_core_interface_1_nr_o[1]),
    .L1_o(caclulating_core_interface_1_nr_o[2]), .E1_o(caclulating_core_interface_1_nr_o[3]),
    .Src1__eq__Dest(caclulating_core_interface_1_nr_o[4]), .Src1(caclulating_core_interface_1_src1),
    .Src2(caclulating_core_interface_1_src2), .Dest(caclulating_core_interface_1_dest),
    .nCMP(caclulating_core_interface_1_nr_o[14]), .Src2_ind(caclulating_core_interface_1_nr_o[15]),
    .ALU_instr(caclulating_core_interface_1_nr_o[16]), .Const(caclulating_core_interface_1_const),
    .Carry(caclulating_core_interface_1_carry[0]), .Const_enable(caclulating_core_interface_1_carry[1]),
    .Sub_Inv_Rev(caclulating_core_interface_1_carry[2]), .Arithm(caclulating_core_interface_1_carry[3]),
    .Enable_C_in_RotC(caclulating_core_interface_1_carry[4]),
    .Function(caclulating_core_interface_1_function), .E2(caclulating_core_interface_1_carry[8]), .nr(nr),
    .clk(Clk), .L1(L1), .E1(E1), .ALU_Step(E2), .MOV_mi(disable_SD), .C_in(Status_Register_flags_out[0]),
    .I_in({Instruction_Register_d_out_2, INSTR_8, Instruction_Register_d_out}));
  Seven_Seg_Hex seven_seg_hex_1 (.d(clk_cnt[7:4]), .dp(1'b0));
  _1_to_8b_extender _1_to_8b_extender_1 (.in(INSTR_8), .out(_1_to_8b_extender_1_out));
  Multiplexer #(.Bits(16)) multiplexer_1 (
    .sel(S5), .in_0(register_file_1_src1_to_bus), .in_1(address_adder_1_out), .out(multiplexer_1_out));
  Seven_Seg_Hex seven_seg_hex_2 (.d(clk_cnt[3:0]), .dp(1'b0));
  Multiplexer #(.Bits(16)) multiplexer_2 (
    .sel(S6), .in_0(register_file_1_src1_to_bus),
    .in_1({_1_to_8b_extender_1_out, Instruction_Register_d_out}), .out(multiplexer_2_out));
  Multiplexer #(.Bits(16)) multiplexer_3 (
    .sel(S5), .in_0(multiplexer_2_out), .in_1(address_adder_1_out_2), .out(multiplexer_3_out));
  Register_file register_file_1 (
    .Src2_out(register_file_1_src2_out), .Src1_out(register_file_1_src1_out),
    .nr(caclulating_core_interface_1_nr_o[0]), .Clk(caclulating_core_interface_1_nr_o[1]),
    .L1(caclulating_core_interface_1_nr_o[2]), .E1(caclulating_core_interface_1_nr_o[3]),
    .Src1_eq_Dest(caclulating_core_interface_1_nr_o[4]), .Src1(src_mod[3:1]),
    .Src2(caclulating_core_interface_1_src2), .Dest(dest_mod[2:0]),
    .nCMP(caclulating_core_interface_1_nr_o[14]), .Src2_ind(caclulating_core_interface_1_nr_o[15]),
    .ALU_instr(caclulating_core_interface_1_nr_o[16]), .D_in(register_file_1_src1_to_bus),
    .gpr7_latch(gpr7_latch), .R0_3(R0_3), .R4_7(R4_7), .LA1_i(LA1_i), .EA1_i(EA1_i), .S1_i(S1_i),
    .S2_i(S2_i), .Src1_to_bus(register_file_1_src1_to_bus));  // open: Reg_write
  Main_ALU_no_indicators main_alu_no_indicators_1 (
    .Src2(register_file_1_src2_out), .Src1(register_file_1_src1_out),
    .Const(caclulating_core_interface_1_const), .Carry_in(caclulating_core_interface_1_carry[0]),
    .Const_enable(caclulating_core_interface_1_carry[1]),
    .Sub_Inv_Rev(caclulating_core_interface_1_carry[2]), .Arithm(caclulating_core_interface_1_carry[3]),
    .Enable_C_in_RotC(caclulating_core_interface_1_carry[4]),
    .Function(caclulating_core_interface_1_function), .ALU_enable(caclulating_core_interface_1_carry[8]),
    .Output(register_file_1_src1_to_bus), .C(main_alu_no_indicators_1_c[0]),
    .O(main_alu_no_indicators_1_c[1]), .N(main_alu_no_indicators_1_c[2]), .Z(main_alu_no_indicators_1_c[3]));  // open: Sum, B_in
  _1_to_16b_extender _1_to_16b_extender_1 (.in(multiplexer_2_out[15]), .out(_1_to_16b_extender_1_out));
  Memory_Pointers MemPointers (
    .nr(nr), .LA34(LA34), .L3(L3), .L4(L4), .D3(multiplexer_3_out), .D4(multiplexer_1_out), .S3(S3), .PC(PC),
    .SP(SP), .FP(FP), .BP(BP), .MP_H(MemPointers_mp_h), .MP_L(MemPointers_mp_l));
  Button #(.activeLow("true")) R (.out(nr));
  not not_1 (nclk, Clk);
  LED u_clk (.in(Clk));
  LED u_nclk (.in(nclk));
  PullUp #(.Bits(16)) pullup_1 (.out(pullup_1_out));
  Seven_Seg_Hex seven_seg_hex_3 (.d(clk_cnt[7:4]), .dp(1'b0));
  not not_2 (not_2_out, nr);
  Seven_Seg_Hex seven_seg_hex_4 (.d(ROM_address), .dp(1'b0));
  Seven_Seg_Hex seven_seg_hex_5 (.d(clk_cnt[3:0]), .dp(1'b0));
  Counter #(.Bits(8)) counter_1 (.en(nr), .C(Clk), .clr(not_2_out), .out(clk_cnt));  // open: ovf
  Multiplexer #(.Bits(4)) multiplexer_4 (
    .sel(S7), .in_0(main_alu_no_indicators_1_c), .in_1(register_file_1_src1_to_bus[3:0]),
    .out(multiplexer_4_out));
  assign register_file_1_src1_to_bus = E4 ? multiplexer_5_out : 16'bz;  // Driver driver_1
  Multiplexer #(.Bits(16)) multiplexer_5 (
    .sel(S4), .in_0(MemPointers_mp_h), .in_1(MemPointers_mp_l), .out(multiplexer_5_out));
  LED led_1 (.in(R0_3[15]));
  LED led_2 (.in(R0_3[14]));
  LED led_3 (.in(R0_3[31]));
  LED led_4 (.in(R0_3[30]));
  LED led_5 (.in(R0_3[47]));
  LED led_6 (.in(R0_3[46]));
  LED led_7 (.in(R0_3[63]));
  LED led_8 (.in(R0_3[62]));
  LED led_9 (.in(R4_7[15]));
  LED led_10 (.in(R4_7[14]));
  LED led_11 (.in(R4_7[31]));
  LED led_12 (.in(R4_7[30]));
  LED led_13 (.in(R4_7[47]));
  LED led_14 (.in(R4_7[46]));
  LED led_15 (.in(R4_7[63]));
  LED led_16 (.in(R4_7[62]));
  LED led_17 (.in(R0_3[13]));
  LED led_18 (.in(R0_3[12]));
  LED led_19 (.in(R0_3[11]));
  LED led_20 (.in(R0_3[10]));
  LED led_21 (.in(R0_3[29]));
  LED led_22 (.in(R0_3[28]));
  LED led_23 (.in(R0_3[27]));
  LED led_24 (.in(R0_3[26]));
  LED led_25 (.in(R0_3[45]));
  LED led_26 (.in(R0_3[44]));
  LED led_27 (.in(R0_3[43]));
  LED led_28 (.in(R0_3[42]));
  LED led_29 (.in(R0_3[61]));
  LED led_30 (.in(R0_3[60]));
  LED led_31 (.in(R0_3[59]));
  LED led_32 (.in(R0_3[58]));
  LED led_33 (.in(R4_7[13]));
  LED led_34 (.in(R4_7[12]));
  LED led_35 (.in(R4_7[11]));
  LED led_36 (.in(R4_7[10]));
  LED led_37 (.in(R4_7[29]));
  LED led_38 (.in(R4_7[28]));
  LED led_39 (.in(R4_7[27]));
  LED led_40 (.in(R4_7[26]));
  LED led_41 (.in(R4_7[45]));
  LED led_42 (.in(R4_7[44]));
  LED led_43 (.in(R4_7[43]));
  LED led_44 (.in(R4_7[42]));
  LED led_45 (.in(R4_7[61]));
  LED led_46 (.in(R4_7[60]));
  LED led_47 (.in(R4_7[59]));
  LED led_48 (.in(R4_7[58]));
  LED led_49 (.in(Instruction_Register_d_out_2[15]));
  LED led_50 (.in(Instruction_Register_d_out_2[14]));
  LED led_51 (.in(Instruction_Register_d_out_2[13]));
  LED led_52 (.in(Instruction_Register_d_out_2[12]));
  Flags_Register_8bit Status_Register (
    .nR(nr), .Flags_in(multiplexer_4_out), .Clk(L2), .Flags_out(Status_Register_flags_out));
  LED led_53 (.in(R0_3[9]));
  LED led_54 (.in(R0_3[8]));
  LED led_55 (.in(R0_3[7]));
  LED led_56 (.in(R0_3[6]));
  LED led_57 (.in(R0_3[25]));
  LED led_58 (.in(R0_3[24]));
  LED led_59 (.in(R0_3[23]));
  LED led_60 (.in(R0_3[22]));
  LED led_61 (.in(R0_3[41]));
  LED led_62 (.in(R0_3[40]));
  LED led_63 (.in(R0_3[39]));
  LED led_64 (.in(R0_3[38]));
  LED led_65 (.in(R0_3[57]));
  LED led_66 (.in(R0_3[56]));
  LED led_67 (.in(R0_3[55]));
  LED led_68 (.in(R0_3[54]));
  LED led_69 (.in(R4_7[9]));
  LED led_70 (.in(R4_7[8]));
  LED led_71 (.in(R4_7[7]));
  LED led_72 (.in(R4_7[6]));
  LED led_73 (.in(R4_7[25]));
  LED led_74 (.in(R4_7[24]));
  LED led_75 (.in(R4_7[23]));
  LED led_76 (.in(R4_7[22]));
  LED led_77 (.in(R4_7[41]));
  LED led_78 (.in(R4_7[40]));
  LED led_79 (.in(R4_7[39]));
  LED led_80 (.in(R4_7[38]));
  LED led_81 (.in(R4_7[57]));
  LED led_82 (.in(R4_7[56]));
  LED led_83 (.in(R4_7[55]));
  LED led_84 (.in(R4_7[54]));
  Multiplexer #(.Bits(16)) multiplexer_6 (.sel(S0), .in_0(bus), .in_1(16'h1f01), .out(multiplexer_6_out));
  LED led_85 (.in(Instruction_Register_d_out_2[11]));
  LED led_86 (.in(Instruction_Register_d_out_2[10]));
  LED led_87 (.in(Instruction_Register_d_out_2[9]));
  LED led_88 (.in(INSTR_8));
  Multiplexer #(.Bits(32)) multiplexer_7 (
    .sel(S8), .in_0({MemPointers_mp_h, MemPointers_mp_l}), .in_1(MABH_d_out), .out(multiplexer_7_out));
  LED led_89 (.in(R0_3[5]));
  LED led_90 (.in(R0_3[4]));
  LED led_91 (.in(R0_3[3]));
  LED led_92 (.in(R0_3[2]));
  LED led_93 (.in(R0_3[21]));
  LED led_94 (.in(R0_3[20]));
  LED led_95 (.in(R0_3[19]));
  LED led_96 (.in(R0_3[18]));
  LED led_97 (.in(R0_3[37]));
  LED led_98 (.in(R0_3[36]));
  LED led_99 (.in(R0_3[35]));
  LED led_100 (.in(R0_3[34]));
  LED led_101 (.in(R0_3[53]));
  LED led_102 (.in(R0_3[52]));
  LED led_103 (.in(R0_3[51]));
  LED led_104 (.in(R0_3[50]));
  LED led_105 (.in(R4_7[5]));
  LED led_106 (.in(R4_7[4]));
  LED led_107 (.in(R4_7[3]));
  LED led_108 (.in(R4_7[2]));
  LED led_109 (.in(R4_7[21]));
  LED led_110 (.in(R4_7[20]));
  LED led_111 (.in(R4_7[19]));
  LED led_112 (.in(R4_7[18]));
  LED led_113 (.in(R4_7[37]));
  LED led_114 (.in(R4_7[36]));
  LED led_115 (.in(R4_7[35]));
  LED led_116 (.in(R4_7[34]));
  LED led_117 (.in(R4_7[53]));
  LED led_118 (.in(R4_7[52]));
  LED led_119 (.in(R4_7[51]));
  LED led_120 (.in(R4_7[50]));
  LED led_121 (.in(Instruction_Register_d_out[7]));
  LED led_122 (.in(Instruction_Register_d_out[6]));
  LED led_123 (.in(Instruction_Register_d_out[5]));
  LED led_124 (.in(Instruction_Register_d_out[4]));
  not not_3 (not_3_out[1], Byte);
  LED led_125 (.in(R0_3[1]));
  LED led_126 (.in(R0_3[0]));
  LED led_127 (.in(R0_3[17]));
  LED led_128 (.in(R0_3[16]));
  LED led_129 (.in(R0_3[33]));
  LED led_130 (.in(R0_3[32]));
  LED led_131 (.in(R0_3[49]));
  LED led_132 (.in(R0_3[48]));
  LED led_133 (.in(R4_7[1]));
  LED led_134 (.in(R4_7[0]));
  LED led_135 (.in(R4_7[17]));
  LED led_136 (.in(R4_7[16]));
  LED led_137 (.in(R4_7[33]));
  LED led_138 (.in(R4_7[32]));
  LED led_139 (.in(R4_7[49]));
  LED led_140 (.in(R4_7[48]));
  Register Instruction_Register (
    .nR(nr), .D_in(multiplexer_6_out), .Clk(L0),
    .D_out({Instruction_Register_d_out_2, INSTR_8, Instruction_Register_d_out}));
  LED led_141 (.in(Instruction_Register_d_out[3]));
  LED led_142 (.in(Instruction_Register_d_out[2]));
  LED led_143 (.in(Instruction_Register_d_out[1]));
  LED led_144 (.in(Instruction_Register_d_out[0]));
  LED led_145 (.in(Status_Register_flags_out[0]));
  LED led_146 (.in(Status_Register_flags_out[1]));
  LED led_147 (.in(Status_Register_flags_out[2]));
  LED led_148 (.in(Status_Register_flags_out[3]));
  LED led_149 (.in(MABH_d_out[31]));
  Multiplexer #(.Bits(32)) multiplexer_8 (
    .sel(S11), .in_0(multiplexer_7_out), .in_1({{8{1'b0}}, int_number_d_out, IV_base_d_out}),
    .out(multiplexer_8_out));
  Multiplexer #(.Selector_Bits(2), .Bits(32)) multiplexer_9 (
    .sel(S9), .in_0({32{1'b0}}), .in_1({{30{1'b0}}, not_3_out[1], Byte}), .in_2(32'hfffffffc),
    .in_3({_1_to_16b_extender_1_out, multiplexer_2_out}), .out(multiplexer_9_out));
  LED led_150 (.in(MABH_d_out[30]));
  LED led_151 (.in(MABH_d_out[29]));
  LED led_152 (.in(MABH_d_out[28]));
  LED led_153 (.in(MABH_d_out[27]));
  LED led_154 (.in(PC[31]));
  LED led_155 (.in(PC[30]));
  LED led_156 (.in(PC[29]));
  LED led_157 (.in(PC[28]));
  LED led_158 (.in(SP[31]));
  LED led_159 (.in(SP[30]));
  LED led_160 (.in(SP[29]));
  LED led_161 (.in(SP[28]));
  LED led_162 (.in(FP[31]));
  LED led_163 (.in(FP[30]));
  LED led_164 (.in(FP[29]));
  LED led_165 (.in(FP[28]));
  LED led_166 (.in(BP[31]));
  LED led_167 (.in(BP[30]));
  LED led_168 (.in(BP[29]));
  LED led_169 (.in(BP[28]));
  Address_Adder address_adder_1 (
    .A(multiplexer_8_out), .B(multiplexer_9_out), .out({address_adder_1_out_2, address_adder_1_out}));  // open: Carry
  LED led_170 (.in(MABH_d_out[26]));
  LED led_171 (.in(MABH_d_out[25]));
  LED led_172 (.in(MABH_d_out[24]));
  LED led_173 (.in(MABH_d_out[23]));
  LED led_174 (.in(PC[27]));
  LED led_175 (.in(PC[26]));
  LED led_176 (.in(PC[25]));
  LED led_177 (.in(PC[24]));
  LED led_178 (.in(SP[27]));
  LED led_179 (.in(SP[26]));
  LED led_180 (.in(SP[25]));
  LED led_181 (.in(SP[24]));
  LED led_182 (.in(FP[27]));
  LED led_183 (.in(FP[26]));
  LED led_184 (.in(FP[25]));
  LED led_185 (.in(FP[24]));
  LED led_186 (.in(BP[27]));
  LED led_187 (.in(BP[26]));
  LED led_188 (.in(BP[25]));
  LED led_189 (.in(BP[24]));
  assign register_file_1_src1_to_bus = E3 ? {{12{1'b0}}, Status_Register_flags_out} : 16'bz;  // Driver driver_2
  LED led_190 (.in(MABH_d_out[22]));
  LED led_191 (.in(MABH_d_out[21]));
  LED led_192 (.in(MABH_d_out[20]));
  LED led_193 (.in(MABH_d_out[19]));
  LED led_194 (.in(PC[23]));
  LED led_195 (.in(PC[22]));
  LED led_196 (.in(PC[21]));
  LED led_197 (.in(PC[20]));
  LED led_198 (.in(SP[23]));
  LED led_199 (.in(SP[22]));
  LED led_200 (.in(SP[21]));
  LED led_201 (.in(SP[20]));
  LED led_202 (.in(FP[23]));
  LED led_203 (.in(FP[22]));
  LED led_204 (.in(FP[21]));
  LED led_205 (.in(FP[20]));
  LED led_206 (.in(BP[23]));
  LED led_207 (.in(BP[22]));
  LED led_208 (.in(BP[21]));
  LED led_209 (.in(BP[20]));
  // Sequencer sequencer_1: pin names not known; wires that end beside it: nr, {Instruction_Register_d_out_2, INSTR_8, Instruction_Register_d_out}, Clk, clk_stop, prefix, sequencer_1_p6, Status_Register_flags_out, sequencer_1_p8, sequencer_1_p9, sequencer_1_p10, sequencer_1_p11, sequencer_1_p12, sequencer_1_p13, sequencer_1_p14, sequencer_1_p15, sequencer_1_p16, sequencer_1_p17, sequencer_1_p18, sequencer_1_p19, sequencer_1_p20, sequencer_1_p21, sequencer_1_p22, sequencer_1_p23, src_mod
  // Microinstruction_decoder microinstruction_decoder_1: pin names not known; wires that end beside it: Clk, src_mod, dest_mod, {Instruction_Register_d_out_2, INSTR_8, Instruction_Register_d_out}, sequencer_1_p8, sequencer_1_p9, sequencer_1_p10, sequencer_1_p11, sequencer_1_p12, sequencer_1_p13, sequencer_1_p14, sequencer_1_p16, sequencer_1_p17, sequencer_1_p18, sequencer_1_p19, sequencer_1_p20, sequencer_1_p21, sequencer_1_p22, sequencer_1_p23, {S12, S11, S10, S9, S8, S7, S6, S5, S4, S3, S0}, {en, E6, E5, E4, E3, E2, E1}, {latch[11], L8, L7, L6, L5, L4, L3, LA34, L2, L1, L0}, disable_SD
  LED led_210 (.in(MABH_d_out[15]));
  LED led_211 (.in(MABH_d_out[18]));
  LED led_212 (.in(MABH_d_out[17]));
  LED led_213 (.in(MABH_d_out[16]));
  LED led_214 (.in(PC[19]));
  LED led_215 (.in(PC[18]));
  LED led_216 (.in(PC[17]));
  LED led_217 (.in(PC[16]));
  LED led_218 (.in(SP[19]));
  LED led_219 (.in(SP[18]));
  LED led_220 (.in(SP[17]));
  LED led_221 (.in(SP[16]));
  LED led_222 (.in(FP[19]));
  LED led_223 (.in(FP[18]));
  LED led_224 (.in(FP[17]));
  LED led_225 (.in(FP[16]));
  LED led_226 (.in(BP[19]));
  LED led_227 (.in(BP[18]));
  LED led_228 (.in(BP[17]));
  LED led_229 (.in(BP[16]));
  LED led_230 (.in(MABH_d_out[14]));
  LED led_231 (.in(MABH_d_out[13]));
  LED led_232 (.in(MABH_d_out[12]));
  LED led_233 (.in(MABH_d_out[11]));
  LED led_234 (.in(PC[15]));
  LED led_235 (.in(PC[14]));
  LED led_236 (.in(PC[13]));
  LED led_237 (.in(PC[12]));
  LED led_238 (.in(SP[15]));
  LED led_239 (.in(SP[14]));
  LED led_240 (.in(SP[13]));
  LED led_241 (.in(SP[12]));
  LED led_242 (.in(FP[15]));
  LED led_243 (.in(FP[14]));
  LED led_244 (.in(FP[13]));
  LED led_245 (.in(FP[12]));
  LED led_246 (.in(BP[15]));
  LED led_247 (.in(BP[14]));
  LED led_248 (.in(BP[13]));
  LED led_249 (.in(BP[12]));
  Delay #(.delayTime(4)) delay_1 (.in(L5), .out(delay_1_out));
  LED led_250 (.in(MABH_d_out[10]));
  LED led_251 (.in(MABH_d_out[9]));
  LED led_252 (.in(MABH_d_out[8]));
  LED led_253 (.in(MABH_d_out[7]));
  LED led_254 (.in(PC[11]));
  LED led_255 (.in(PC[10]));
  LED led_256 (.in(PC[9]));
  LED led_257 (.in(PC[8]));
  LED led_258 (.in(SP[11]));
  LED led_259 (.in(SP[10]));
  LED led_260 (.in(SP[9]));
  LED led_261 (.in(SP[8]));
  LED led_262 (.in(FP[11]));
  LED led_263 (.in(FP[10]));
  LED led_264 (.in(FP[9]));
  LED led_265 (.in(FP[8]));
  LED led_266 (.in(BP[11]));
  LED led_267 (.in(BP[10]));
  LED led_268 (.in(BP[9]));
  LED led_269 (.in(BP[8]));
  LED led_270 (.in(sequencer_1_p15[3]));
  LED led_271 (.in(sequencer_1_p15[2]));
  LED led_272 (.in(sequencer_1_p15[1]));
  Register MABH (.nR(nr), .D_in(address_adder_1_out), .Clk(delay_1_out), .D_out(MABH_d_out[15:0]));
  Register MABL (.nR(nr), .D_in(address_adder_1_out_2), .Clk(delay_1_out), .D_out(MABH_d_out[31:16]));
  LED led_273 (.in(MABH_d_out[6]));
  LED led_274 (.in(MABH_d_out[5]));
  LED led_275 (.in(MABH_d_out[4]));
  LED led_276 (.in(MABH_d_out[3]));
  LED led_277 (.in(PC[7]));
  LED led_278 (.in(PC[6]));
  LED led_279 (.in(PC[5]));
  LED led_280 (.in(PC[4]));
  LED led_281 (.in(SP[7]));
  LED led_282 (.in(SP[6]));
  LED led_283 (.in(SP[5]));
  LED led_284 (.in(SP[4]));
  LED led_285 (.in(FP[7]));
  LED led_286 (.in(FP[6]));
  LED led_287 (.in(FP[5]));
  LED led_288 (.in(FP[4]));
  LED led_289 (.in(BP[7]));
  LED led_290 (.in(BP[6]));
  LED led_291 (.in(BP[5]));
  LED led_292 (.in(BP[4]));
  LED led_293 (.in(sequencer_1_p15[0]));
  LED led_294 (.in(MDB_d_out[15]));
  LED led_295 (.in(MDB_d_out[14]));
  LED led_296 (.in(MDB_d_out[13]));
  LED led_297 (.in(MDB_d_out[12]));
  LED led_298 (.in(MABH_d_out[2]));
  LED led_299 (.in(MABH_d_out[1]));
  LED led_300 (.in(MABH_d_out[0]));
  LED led_301 (.in(PC[3]));
  LED led_302 (.in(PC[2]));
  LED led_303 (.in(PC[1]));
  LED led_304 (.in(PC[0]));
  LED led_305 (.in(SP[3]));
  LED led_306 (.in(SP[2]));
  LED led_307 (.in(SP[1]));
  LED led_308 (.in(SP[0]));
  LED led_309 (.in(FP[3]));
  LED led_310 (.in(FP[2]));
  LED led_311 (.in(FP[1]));
  LED led_312 (.in(FP[0]));
  LED led_313 (.in(BP[3]));
  LED led_314 (.in(BP[2]));
  LED led_315 (.in(BP[1]));
  LED led_316 (.in(BP[0]));
  LED led_317 (.in(MDB_d_out[11]));
  LED led_318 (.in(MDB_d_out[10]));
  LED led_319 (.in(MDB_d_out[9]));
  LED led_320 (.in(MDB_d_out[8]));
  LED led_321 (.in(MDB_d_out[7]));
  LED led_322 (.in(MDB_d_out[6]));
  LED led_323 (.in(MDB_d_out[5]));
  LED led_324 (.in(MDB_d_out[4]));
  LED NOP (.in(undriven));
  LED led_325 (.in(MDB_d_out[3]));
  LED led_326 (.in(MDB_d_out[2]));
  LED led_327 (.in(MDB_d_out[1]));
  LED led_328 (.in(MDB_d_out[0]));
  Multiplexer #(.Bits(8)) multiplexer_10 (
    .sel(S12), .in_0(Instruction_Register_d_out), .in_1(\int ), .out(multiplexer_10_out));
  Button Int_mock (.out(Int_mock_out));
  or or_1 (dis_addr_set, disable_SD, in_4);
  Register MDB (.nR(nr), .D_in(register_file_1_src1_to_bus), .Clk(L6), .D_out(MDB_d_out));
  Register IV_base (.nR(nr), .D_in(register_file_1_src1_to_bus), .Clk(L8), .D_out(IV_base_d_out));
  Register_8bit int_number (.nR(nr), .D_in(multiplexer_10_out), .Clk(L7), .D_out(int_number_d_out));
  LED led_329 (.in(int_number_d_out[7]));
  LED led_330 (.in(int_number_d_out[6]));
  LED led_331 (.in(int_number_d_out[5]));
  not not_4 (not_4_out, S0);
  LED led_332 (.in(int_number_d_out[4]));
  LED led_333 (.in(int_number_d_out[3]));
  LED led_334 (.in(int_number_d_out[2]));
  LED led_335 (.in(int_number_d_out[1]));
  or or_2 (or_2_out, Soft_Int, Int_mock_out);
  not not_5 (not_5_out, not_4_out);
  assign register_file_1_src1_to_bus = E5 ? MDB_d_out : 16'bz;  // Driver driver_3
  LED led_336 (.in(IV_base_d_out[15]));
  LED led_337 (.in(int_number_d_out[0]));
  not not_6 (not_6_out, or_2_out);
  and and_1 (and_1_out, not_4_out, not_5_out);
  _1_to_8b_extender _1_to_8b_extender_2 (.in(Instruction_Register_d_out[7]), .out(_1_to_8b_extender_2_out));
  LED led_338 (.in(IV_base_d_out[14]));
  LED led_339 (.in(IV_base_d_out[13]));
  LED led_340 (.in(IV_base_d_out[12]));
  LED led_341 (.in(IV_base_d_out[11]));
  not not_7 (not_7_out, not_6_out);
  LED led_342 (.in(S0));
  LED led_343 (.in(S3[0]));
  LED led_344 (.in(S3[1]));
  LED led_345 (.in(S4));
  LED led_346 (.in(S5));
  LED led_347 (.in(S6));
  LED led_348 (.in(S7));
  LED led_349 (.in(S8));
  LED led_350 (.in(S9[0]));
  LED led_351 (.in(S9[1]));
  LED led_352 (.in(S10[0]));
  LED led_353 (.in(S10[1]));
  LED led_354 (.in(S11));
  LED led_355 (.in(S12));
  assign register_file_1_src1_to_bus = en[6] ? bus : 16'bz;  // Driver driver_4
  assign bus = en[7] ? register_file_1_src1_to_bus : 16'bz;  // Driver driver_5
  LED led_356 (.in(IV_base_d_out[10]));
  LED led_357 (.in(IV_base_d_out[9]));
  LED led_358 (.in(IV_base_d_out[8]));
  LED led_359 (.in(IV_base_d_out[7]));
  D_FF_AS u_Int (.Set(1'b0), .D(or_2_out), .C(not_7_out), .Clr(and_1_out), .Q(sequencer_1_p6));  // open: nQ
  LED led_360 (.in(IV_base_d_out[6]));
  LED led_361 (.in(IV_base_d_out[5]));
  LED led_362 (.in(IV_base_d_out[4]));
  LED led_363 (.in(IV_base_d_out[3]));
  LED led_364 (.in(sequencer_1_p6));
  LED led_365 (.in(IV_base_d_out[2]));
  LED led_366 (.in(IV_base_d_out[1]));
  LED led_367 (.in(IV_base_d_out[0]));
  Multiplexer #(.Selector_Bits(2), .Bits(32)) multiplexer_11 (
    .sel(S10), .in_0({MemPointers_mp_h, MemPointers_mp_l}), .in_1(MABH_d_out),
    .in_2({_1_to_8b_extender_2_out[6:0], Instruction_Register_d_out, MDB_d_out, 1'b0}), .in_3(DMA),
    .out({multiplexer_11_out[31:5], ROM_address, multiplexer_11_out[0]}));
  LED led_368 (.in(E1));
  LED led_369 (.in(E2));
  LED led_370 (.in(E3));
  LED led_371 (.in(E4));
  LED led_372 (.in(E5));
  LED u_E6 (.in(E6));
  LED led_373 (.in(en[6]));
  LED led_374 (.in(en[7]));
  T_B_sel t_b_sel_1 (.Flip(1'b0), .in(multiplexer_11_out[31:24]), .bottom(t_b_sel_1_bottom));  // open: top
  LED led_375 (.in(multiplexer_11_out[31]));
  LED led_376 (.in(multiplexer_11_out[30]));
  LED led_377 (.in(multiplexer_11_out[29]));
  LED led_378 (.in(multiplexer_11_out[28]));
  LED led_379 (.in(L0));
  LED u_L1 (.in(L1));
  LED led_380 (.in(L2));
  LED led_381 (.in(LA34[0]));
  LED led_382 (.in(LA34[1]));
  LED led_383 (.in(L3));
  LED led_384 (.in(L4));
  LED u_L5 (.in(L5));
  LED led_385 (.in(L6));
  LED led_386 (.in(L7));
  LED led_387 (.in(L8));
  LED W (.in(latch[11]));
  PullUp pullup_2 (.out(pullup_2_out));
  not not_8 (not_8_out, latch[11]);
  LED led_388 (.in(multiplexer_11_out[27]));
  LED led_389 (.in(multiplexer_11_out[26]));
  LED led_390 (.in(multiplexer_11_out[25]));
  LED led_391 (.in(multiplexer_11_out[24]));
  RAMSinglePortSel #(.AddrBits(23), .Bits(16)) _16MB_RAM (
    .A({multiplexer_11_out[23:5], ROM_address}), .CS(t_b_sel_1_bottom), .WE(latch[11]), .OE(not_8_out),
    .D(_16MB_RAM_d));
  LED led_392 (.in(multiplexer_11_out[23]));
  LED led_393 (.in(multiplexer_11_out[22]));
  LED led_394 (.in(multiplexer_11_out[21]));
  LED led_395 (.in(multiplexer_11_out[20]));
  LED led_396 (.in(multiplexer_11_out[19]));
  LED led_397 (.in(multiplexer_11_out[18]));
  LED led_398 (.in(multiplexer_11_out[17]));
  LED led_399 (.in(multiplexer_11_out[16]));
  LED led_400 (.in(multiplexer_11_out[15]));
  LED led_401 (.in(multiplexer_11_out[14]));
  LED led_402 (.in(multiplexer_11_out[13]));
  LED led_403 (.in(multiplexer_11_out[12]));
  LED led_404 (.in(multiplexer_11_out[11]));
  LED led_405 (.in(multiplexer_11_out[10]));
  LED led_406 (.in(multiplexer_11_out[9]));
  LED led_407 (.in(multiplexer_11_out[8]));
  EEPROM #(.AddrBits(4), .Bits(16)) ROM (.A(ROM_address), .CS(pullup_2_out), .WE(latch[11]), .OE(E6), .D(bus));
  LED led_408 (.in(multiplexer_11_out[7]));
  LED led_409 (.in(multiplexer_11_out[6]));
  LED led_410 (.in(multiplexer_11_out[5]));
  LED led_411 (.in(ROM_address[3]));
  LED led_412 (.in(ROM_address[2]));
  LED led_413 (.in(ROM_address[1]));
  LED led_414 (.in(ROM_address[0]));
  LED led_415 (.in(multiplexer_11_out[0]));
  Seven_Seg_Hex seven_seg_hex_6 (.d(clk_cnt[7:4]), .dp(1'b0));
  Seven_Seg_Hex seven_seg_hex_7 (.d(clk_cnt[3:0]), .dp(1'b0));

  // Other names for the same wires on the sheet: en[5:0] = {E6, E5, E4, E3, E2, E1}; T1 = en[6]; T2 = en[7];
  //   latch[10:0] = {L8, L7, L6, L5, L4, L3, LA34, L2, L1, L0}; W = latch[11];
  //   sel[13:0] = {S12, S11, S10, S9, S8, S7, S6, S5, S4, S3, S0}

  // Notes on the sheet:
  //   int: from interrupt controller
  //   Calculating core
  //   Const (8bit)
  //   Data bus (16bit)
  //   Flags (C,O,N,Z)
  //   ECM-16/TTL cpu
  //   C
  //   O
  //   N
  //   Z
  //   Fetch EINT === int ack
  //   Interrupt controller mock
  //   Data/Instr bus (16bit)
  //   S0
  //   S3_0
  //   S3_1
  //   S4
  //   S5
  //   S6
  //   S7
  //   S8
  //   S9_0
  //   S9_1
  //   S10_0
  //   S10_1
  //   S11
  //   S12
  //   E1
  //   E2
  //   E3
  //   E4
  //   E5
  //   E6
  //   T1
  //   T2
  //   LA3_0
  //   LA3_1
  //   L0
  //   L1
  //   L2
  //   L3
  //   L4
  //   L5
  //   L6
  //   L7
  //   L8
  //   W
  //   contents of ROM (hex, n*v repeats v):
  //   8814,5000,f,4f00,f,8b1f,7303,6703,0,0,1f,f000,0,0,0,14
endmodule
